# Fritzing sketch 接线图 (saved by Fritzing 0.9.3b)
breadboards: 1

parts:
  元件1 = Arduino BT
  LED2 = LED - 5mm [color="Green (570nm)" package="5 mm [THT]"]
  LED3 = LED - 5mm [color="Green (570nm)" package="5 mm [THT]"]
  LED4 = LED - 5mm [color="Green (570nm)" package="5 mm [THT]"]
  LED5 = LED - 5mm [color="Green (570nm)" package="5 mm [THT]"]
  LED6 = LED - 5mm [color="Green (570nm)" package="5 mm [THT]"]
  LED7 = LED - 5mm [color="Green (570nm)" package="5 mm [THT]"]
  LED8 = LED - 5mm [color="Green (570nm)" package="5 mm [THT]"]
  LED1 = LED - 5mm [color="Green (570nm)" package="5 mm [THT]"]
  R1 = Resistor [tolerance=±5% resistance=220 package=THT]
  R2 = Resistor [tolerance=±5% resistance=220 package=THT]
  R3 = Resistor [tolerance=±5% resistance=220 package=THT]
  R4 = Resistor [tolerance=±5% resistance=220 package=THT]
  R5 = Resistor [tolerance=±5% resistance=220 package=THT]
  R6 = Resistor [tolerance=±5% resistance=220 package=THT]
  R7 = Resistor [tolerance=±5% resistance=220 package=THT]
  R9 = Resistor [tolerance=±5% resistance=220 package=THT]
  RE1 = Rotary Encoder [package=THT]
  RE2 = Rotary Encoder [package=THT]
  RE3 = Rotary Encoder [package=THT]
  RE4 = Rotary Encoder [package=THT]
  RE5 = Rotary Encoder [package=THT]
  RE6 = Rotary Encoder [package=THT]
  RE7 = Rotary Encoder [package=THT]
  RE8 = Rotary Encoder [package=THT]
  R10 = Resistor [tolerance=±5% resistance=220 package=THT]
  R11 = Resistor [tolerance=±5% resistance=220 package=THT]
  R12 = Resistor [tolerance=±5% resistance=220 package=THT]
  R13 = Resistor [tolerance=±5% resistance=220 package=THT]
  R14 = Resistor [tolerance=±5% resistance=220 package=THT]
  R15 = Resistor [tolerance=±5% resistance=220 package=THT]
  R16 = Resistor [tolerance=±5% resistance=220 package=THT]
  R17 = Resistor [tolerance=±5% resistance=220 package=THT]
  SPKR1 = Loudspeaker

nets:
  N1: 元件1.D8, R15.Pin_0
  N2: 元件1.PWM_D9, R16.Pin_0
  N3: 元件1.SS/PWM_D10, R12.Pin_0
  N4: 元件1.MOSI/PWM_D11, R14.Pin_0
  N5: 元件1.MISO/D12, R11.Pin_0
  N6: 元件1.SCK/D13, R10.Pin_0
  N7: 元件1.GND, RE8.EncoderPinB, R13.Pin_0, SPKR1.pin1
  N8: 元件1.AREF, LED2.cathode, LED4.cathode, LED5.cathode, LED7.cathode, LED8.cathode, RE1.EncoderPinA, RE2.EncoderPinA, RE3.EncoderPinA, RE4.EncoderPinA, RE5.EncoderPinA, RE6.EncoderPinA, RE7.EncoderPinA, RE8.EncoderPinA
  N9: 元件1.A0, RE6.EncoderPinB
  N10: 元件1.A1, RE5.EncoderPinB
  N11: 元件1.A2, RE4.EncoderPinB
  N12: 元件1.A3, RE3.EncoderPinB
  N13: 元件1.A4, RE2.EncoderPinB
  N14: 元件1.A5, RE1.EncoderPinB
  N15: 元件1.RX/D0, R1.Pin_0
  N16: 元件1.TX/D1, R2.Pin_0
  N17: 元件1.D2, R3.Pin_0
  N18: 元件1.PWM_D3, R5.Pin_0
  N19: 元件1.D4, R4.Pin_0
  N20: 元件1.PWM_D5, R6.Pin_0
  N21: 元件1.PWM_D6, R7.Pin_0
  N22: 元件1.RESET_WT11/D7, R9.Pin_0
  N23: 元件1.VIN, RE7.EncoderPinB
  N24: 元件1.5V, SPKR1.pin2
  N25: LED2.anode, R4.Pin_1
  N26: LED3.anode, R2.Pin_1
  N27: LED4.anode, R7.Pin_1
  N28: LED5.anode, R3.Pin_1
  N29: LED6.anode, R6.Pin_1
  N30: LED7.anode, R5.Pin_1
  N31: LED8.anode, R9.Pin_1
  N32: LED1.anode, R1.Pin_1
  N33: RE1.EncoderPinC, R17.Pin_1
  N34: RE2.EncoderPinC, R15.Pin_1
  N35: RE3.EncoderPinC, R16.Pin_1
  N36: RE4.EncoderPinC, R12.Pin_1
  N37: RE5.EncoderPinC, R14.Pin_1
  N38: RE6.EncoderPinC, R11.Pin_1
  N39: RE7.EncoderPinC, R10.Pin_1
  N40: RE8.EncoderPinC, R13.Pin_1
